# Fritzing sketch Skema Rangkaian (saved by Fritzing 0.9.3b)

parts:
  U2 = NodeMCU V1.0
  부품3 = FC-28 Soil Hygrometer Module - Probe
  부품4 = FC-28 Soil Hygrometer Module
  Mod2 = KY-015 Temperature & Humidity Sensor Module [package="Breakout board"]  # not connected
  Mod3 = KY-015 Temperature & Humidity Sensor Module [package="Breakout board"]

nets:
  N1: U2.D1, Mod3.S
  3V3: U2.3V3, 부품4.VCC, Mod3.Vin
  GND: U2.GND, 부품4.GND, Mod3.-
  N2: U2.A0, 부품4.AO
  N3: 부품3.POS, 부품4.POS
  N4: 부품3.NEG, 부품4.NEG

custom parts:
  NodeMCU V1.0: ESP8266 based NodeMCU
  FC-28 Soil Hygrometer Module - Probe: The FC-28 is a soil hygrometer module that uses the Texas Instruments LM393 comparator chip to provide an analog measurement of soil humidity.
  FC-28 Soil Hygrometer Module: The FC-28 is a soil hygrometer module that uses the Texas Instruments LM393 comparator chip to provide an analog measurement of soil humidity. The digital output is high when soil moisture is over a certain threshold, as determined by adjusting the potentiometer.
  KY-015 Temperature & Humidity Sensor Module: KY-015 temperature and humidity sensor module, provides a low-latency serial interface to measure humidity and temperature.
